// Logisim project AMU.circ as structural Verilog: 1 circuit, main circuit AMU
module AMU (
  input  [31:0] Input_1,
  input  [31:0] input_2,
  input  Enable,
  input  [2:0] AMU_select,
  output [31:0] AMU_out
);

  wire [31:0] adder_1_out, and_1_out, or_1_out, subtractor_1_out;

  assign and_1_out = input_2 & Input_1;  // AND_Gate and_1, 32 bits wide
  assign or_1_out = input_2 | Input_1;  // OR_Gate or_1, 32 bits wide
  Adder #(.width(32)) adder_1 (.a(Input_1), .b(input_2), .out(adder_1_out), .cin(1'b0));  // open: cout
  Subtractor #(.width(32)) subtractor_1 (.a(Input_1), .b(input_2), .out(subtractor_1_out), .bin(1'b0));  // open: bout
  Multiplexer #(.select(3), .width(32)) multiplexer_1 (
    .in0(adder_1_out), .in1(subtractor_1_out), .in2(and_1_out), .in3(or_1_out), .in4(Input_1),
    .in5(adder_1_out), .in6(adder_1_out), .in7(input_2), .out(AMU_out), .sel(AMU_select), .en(Enable));

  // Notes on the sheet:
  //   Arithematic mathematical Unit(AMU)
endmodule
